// Logisim project CPU.circ as structural Verilog: 1 circuit, main circuit main
module main (
);

  wire and_1_out, and_2_out, Bit1, Bit2, Bit3, Bit4, Bit5, Bit6, Bit7, Bit8, Bit9, Bit10, Bit11, Bit12,
       Bit13, Bit14, Bit15, Bit16, ClockSync, isLDCounter, not_1_out;
  wire [13:0] Operand1Data, Operand2Data;
  wire [15:0] CounterValue, LDCounter;
  wire [63:0] register_1_q, register_2_q, register_3_q;
  wire [63:1] RAMData;

  Clock clock_1 (.out(ClockSync));
  and and_1 (and_1_out, Bit1, Bit2);
  Counter #(.max('hffff), .width(16)) counter_1 (
    .load(isLDCounter), .count(ClockSync), .clk(ClockSync), .D(LDCounter), .Q(CounterValue));  // open: clr, up, carry
  Register #(.width(64)) register_1 (
    .D({RAMData[63:61], Bit16, RAMData[59:57], Bit15, RAMData[55:53], Bit14, RAMData[51:49], Bit13, RAMData[47:45], Bit12, RAMData[43:41], Bit11, RAMData[39:37], Bit10, RAMData[35:33], Bit9, RAMData[31:29], Bit8, RAMData[27:25], Bit7, RAMData[23:21], Bit6, RAMData[19:17], Bit5, RAMData[15:13], Bit4, RAMData[11:9], Bit3, RAMData[7:5], Bit2, RAMData[3:1], Bit1}),
    .en(Bit1), .clk(ClockSync), .Q(register_1_q));  // open: clr
  not not_1 (not_1_out, and_1_out);
  and and_2 (and_2_out, Bit1, Bit2);
  Register #(.width(64)) register_2 (
    .D({RAMData[63:61], Bit16, RAMData[59:57], Bit15, RAMData[55:53], Bit14, RAMData[51:49], Bit13, RAMData[47:45], Bit12, RAMData[43:41], Bit11, RAMData[39:37], Bit10, RAMData[35:33], Bit9, RAMData[31:29], Bit8, RAMData[27:25], Bit7, RAMData[23:21], Bit6, RAMData[19:17], Bit5, RAMData[15:13], Bit4, RAMData[11:9], Bit3, RAMData[7:5], Bit2, RAMData[3:1], Bit1}),
    .en(not_1_out), .clk(ClockSync),
    .Q({register_2_q[63:61], Operand1Data[13], register_2_q[59:57], Operand1Data[12], register_2_q[55:53], Operand1Data[11], register_2_q[51:49], Operand1Data[10], register_2_q[47:45], Operand1Data[9], register_2_q[43:41], Operand1Data[8], register_2_q[39:37], Operand1Data[7], register_2_q[35:33], Operand1Data[6], register_2_q[31:29], Operand1Data[5], register_2_q[27:25], Operand1Data[4], register_2_q[23:21], Operand1Data[3], register_2_q[19:17], Operand1Data[2], register_2_q[15:13], Operand1Data[1], register_2_q[11:9], Operand1Data[0], register_2_q[7:0]}));  // open: clr
  Register #(.width(64)) register_3 (
    .D({RAMData[63:61], Bit16, RAMData[59:57], Bit15, RAMData[55:53], Bit14, RAMData[51:49], Bit13, RAMData[47:45], Bit12, RAMData[43:41], Bit11, RAMData[39:37], Bit10, RAMData[35:33], Bit9, RAMData[31:29], Bit8, RAMData[27:25], Bit7, RAMData[23:21], Bit6, RAMData[19:17], Bit5, RAMData[15:13], Bit4, RAMData[11:9], Bit3, RAMData[7:5], Bit2, RAMData[3:1], Bit1}),
    .en(and_2_out), .clk(ClockSync),
    .Q({register_3_q[63:61], Operand2Data[13], register_3_q[59:57], Operand2Data[12], register_3_q[55:53], Operand2Data[11], register_3_q[51:49], Operand2Data[10], register_3_q[47:45], Operand2Data[9], register_3_q[43:41], Operand2Data[8], register_3_q[39:37], Operand2Data[7], register_3_q[35:33], Operand2Data[6], register_3_q[31:29], Operand2Data[5], register_3_q[27:25], Operand2Data[4], register_3_q[23:21], Operand2Data[3], register_3_q[19:17], Operand2Data[2], register_3_q[15:13], Operand2Data[1], register_3_q[11:9], Operand2Data[0], register_3_q[7:0]}));  // open: clr
  RAM #(.addrWidth(16), .dataWidth(64)) ram_1 (
    .addr(CounterValue), .clk(ClockSync),
    .dout({RAMData[63:61], Bit16, RAMData[59:57], Bit15, RAMData[55:53], Bit14, RAMData[51:49], Bit13, RAMData[47:45], Bit12, RAMData[43:41], Bit11, RAMData[39:37], Bit10, RAMData[35:33], Bit9, RAMData[31:29], Bit8, RAMData[27:25], Bit7, RAMData[23:21], Bit6, RAMData[19:17], Bit5, RAMData[15:13], Bit4, RAMData[11:9], Bit3, RAMData[7:5], Bit2, RAMData[3:1], Bit1}));  // open: we, oe, din

  // Other names for the same wires on the sheet: RAMData (some bits) = {Bit16, Bit15, Bit14, Bit13, Bit12, Bit11, Bit10, Bit9, Bit8, Bit7, Bit6, Bit5, Bit4, Bit3, Bit2, Bit1}

  // Notes on the sheet:
  //   Clock
  //   Decoding Unit
  //   Instruction Register
  //   Program Counter
  //   Opcode Register 1
  //   Opcode Register 1
  //   Count Unit
endmodule
